// Logisim project 16bit_CPU.circ as structural Verilog
module ALU (
  input  [15:0] A,
  input  [15:0] B,
  input  [3:0] AU_Sel,
  output [15:0] AUResult
);

  wire [15:0] adder_1_out;

  Adder #(.width(16)) adder_1 (.a(A), .b(B), .out(adder_1_out));  // open: cin, cout
  Multiplexer #(.select(4), .width(16)) multiplexer_1 (
    .in0(adder_1_out), .out(AUResult), .sel(AU_Sel));  // open: in1, in2, in3, in4, in5, in6, in7, in8, in9, in10, in11, in12, in13, in14, in15
endmodule
